# Fritzing sketch IRTH_circuit (saved by Fritzing 0.9.3b)
breadboards: 1

parts:
  U1 = MLX90614 [package=to-39]
  부품1 = Arduino Nano (Rev3.0)
  LCD2 = LCD screen
  LCM1602_IIC2 = LCM1602 IIC [part_number="LCM1602 IIC" chip_label="LCM1602 IIC" package="DIP (Dual Inline) [THT]"]
  VCC1 = 4 x AAA Battery Mount

nets:
  5V: U1.SCL_VZ, 부품1.5V, LCM1602_IIC2.VCC
  GND: U1.PWM_SDA, 부품1.GND, LCM1602_IIC2.GND, VCC1.-
  N1: U1.VDD, 부품1.A4, LCM1602_IIC2.SDA
  N2: U1.VSS, 부품1.A5, LCM1602_IIC2.SCL
  N3: 부품1.VIN, VCC1.+
  VSS: LCD2.VSS, LCM1602_IIC2.VSS
  N4: LCD2.V0, LCM1602_IIC2.V0
  N5: LCD2.RS, LCM1602_IIC2.RS
  N6: LCD2.R/W, LCM1602_IIC2.RW
  N7: LCD2.E, LCM1602_IIC2.E
  N8: LCD2.DB0, LCM1602_IIC2.D0
  N9: LCD2.DB1, LCM1602_IIC2.D1
  N10: LCD2.DB2, LCM1602_IIC2.D2
  N11: LCD2.DB3, LCM1602_IIC2.D3
  N12: LCD2.DB4, LCM1602_IIC2.D4
  N13: LCD2.DB5, LCM1602_IIC2.D5
  N14: LCD2.DB6, LCM1602_IIC2.D6
  N15: LCD2.DB7, LCM1602_IIC2.D7
  N16: LCD2.LED+, LCM1602_IIC2.A
  N17: LCD2.LED-, LCM1602_IIC2.K

custom parts:
  LCM1602 IIC: I2C-Module to use a 1602 or 2004 LCD on with the wire.h libory Serial LCD Modul
